# Fritzing sketch Alcohol_Detector (saved by Fritzing 0.9.3b)
breadboards: 1

parts:
  WeMos_D1_R1 = WeMos D1 R2
  J1 = Buzzer
  LED1 = smd LED [color="Red (633nm)" package="1206 [SMD]"]
  Part1 = MQ-3 breakout
  R1 = Resistor [tolerance=±5% resistance=220 package=THT]

nets:
  N1: WeMos_D1_R1.GND, J1.pin1
  N2: WeMos_D1_R1.A0, Part1.VCC
  N3: WeMos_D1_R1.5V, Part1.AO
  N4: LED1.cathode, Part1.DO
  N5: LED1.anode, R1.Pin_0

custom parts:
  WeMos D1 R2: The D1 R2 is a mini wifi board based on the ESP-8266EX.
  Buzzer: Fixed frequency buzzer
  MQ-3 breakout: Alcohol sensor is capable of detecting alcohol (ethanol) particles on itself and gives the information in digital form back to us to manipulate with it. SKU:101251 • Voltage: 5V DC • Power: max 750mW • Measurement range: 0.04-4mg/L
